// Logisim project ALU.circ as structural Verilog: 1 circuit, main circuit main
module main (
  input  [2:0] AluCtrl,
  input  [21:0] input1,
  input  [21:0] input2,
  output [21:0] out_4
);

  wire [21:0] adder_1_out, AND_out, divider_1_out, multiplier_1_out, not_1_out, OR_out, subtractor_1_out,
       XOR_out;

  assign XOR_out = input1 ^ input2;  // XOR_Gate XOR, 22 bits wide
  assign OR_out = input1 | input2;  // OR_Gate OR, 22 bits wide
  assign AND_out = input1 & input2;  // AND_Gate AND, 22 bits wide
  Adder #(.width(22)) adder_1 (.a(input1), .b(input2), .out(adder_1_out));  // open: cin, cout
  Subtractor #(.width(22)) subtractor_1 (.a(input1), .b(input2), .out(subtractor_1_out));  // open: bin, bout
  Divider #(.width(22)) divider_1 (.a(input1), .b(input2), .out(divider_1_out));  // open: upper, rem
  Multiplier #(.width(22)) multiplier_1 (.a(input1), .b(input2), .out(multiplier_1_out));  // open: cin, cout
  assign not_1_out = ~input1;  // NOT_Gate not_1, 22 bits wide
  Multiplexer #(.select(3), .width(22), .enable("false")) multiplexer_1 (
    .in0(XOR_out), .in1(OR_out), .in2(AND_out), .in3(adder_1_out), .in4(subtractor_1_out),
    .in5(divider_1_out), .in6(multiplier_1_out), .in7(not_1_out), .out(out_4), .sel(AluCtrl));
endmodule
