// Logisim project ControlUnit.circ as structural Verilog: 1 circuit, main circuit main
module main (
  input  _0,
  input  _1,
  input  _2,
  input  [3:0] funct
);

  wire beq_out, load_out, not_1_out, not_2_out, not_3_out, not_4_out, not_5_out, not_6_out, not_7_out,
       not_8_out, not_9_out, or_1_out, or_2_out, or_3_out, or_4_out, R_type_out, store_out;
  wire [1:0] bit_extender_2_out;
  wire [2:0] bit_extender_1_out, bit_extender_3_out, multiplexer_1_out;

  Bit_Extender #(.in_width(4), .out_width(3)) bit_extender_1 (.in(funct), .out(bit_extender_1_out));
  assign bit_extender_2_out = {{1{or_1_out}}, not_9_out};  // Bit_Extender bit_extender_2
  not not_1 (not_1_out, _0);
  not not_2 (not_2_out, _1);
  and R_type (R_type_out, not_1_out, not_2_out, not_3_out);
  not not_3 (not_3_out, _2);
  not not_4 (not_4_out, _0);
  not not_5 (not_5_out, _1);
  not not_6 (not_6_out, _0);
  and store (store_out, not_6_out, _1, not_7_out);
  not not_7 (not_7_out, _2);
  not not_8 (not_8_out, _0);
  and beq (beq_out, not_8_out, _1, _2);
  and load (load_out, not_4_out, not_5_out, _2);
  not not_9 (not_9_out, beq_out);
  assign bit_extender_3_out = {{1{beq_out}}, bit_extender_2_out};  // Bit_Extender bit_extender_3
  or or_1 (or_1_out, store_out, load_out);
  Multiplexer #(.width(3), .enable("false")) multiplexer_1 (
    .in0(bit_extender_3_out), .in1(bit_extender_1_out), .out(multiplexer_1_out), .sel(R_type_out));
  or or_2 (or_2_out, R_type_out, load_out);
  or or_3 (or_3_out, load_out, store_out);
  or or_4 (or_4_out, load_out, store_out);

  // Notes on the sheet:
  //   OP
  //   ================================
  //   RegDst
  //   RegWrite
  //   AluSrc
  //   ExtOp
  //   MemToReg
  //   MemWrite
  //   Branch
  //   AluCtrl
  //   ====================================
  //   AluControlUnit
  //   MainControlUnit
endmodule
