// Logisim project Mips.circ as structural Verilog: 4 circuits, main circuit DataPath
module DataPath (
  input  in_1,
  input  in_2,
  input  [15:0] PC_1
);

  wire alu_1_euality, Branch_out, clock_1_out, controlunit_1_alusrc, controlunit_1_branch,
       controlunit_1_extop, controlunit_1_jump, controlunit_1_memread, controlunit_1_memtoreg,
       controlunit_1_memwrite, controlunit_1_regdst, controlunit_1_regwrite;
  wire [2:0] controlunit_1_aluctrl, multiplexer_3_out;
  wire [15:0] adder_1_out, adder_2_out, alu_1_alu_output, bit_extender_1_out, bit_extender_2_out,
       bit_extender_3_out, multiplexer_1_out, multiplexer_2_out, multiplexer_4_out, multiplexer_5_out,
       multiplexer_6_out, PC_q, ram_1_data, registerfile_1_outreg1, registerfile_1_outreg2, rom_1_data;

  Clock clock_1 (.out(clock_1_out));
  Register #(.width(16)) PC (.D(multiplexer_1_out), .Q(PC_q), .clk(clock_1_out), .clr(in_1));  // open: en
  Adder #(.width(16)) adder_1 (.a(PC_q), .b(PC_1), .out(adder_1_out));  // open: cin, cout
  Multiplexer #(.width(16), .enable("false")) multiplexer_1 (
    .in0(multiplexer_2_out), .in1(bit_extender_1_out), .out(multiplexer_1_out), .sel(controlunit_1_jump));
  ROM #(.addrWidth(16), .dataWidth(16)) rom_1 (.addr(PC_q), .data(rom_1_data));  // open: sel
  Multiplexer #(.width(16), .enable("false")) multiplexer_2 (
    .in0(adder_1_out), .in1(adder_2_out), .out(multiplexer_2_out), .sel(Branch_out));
  Adder #(.width(16)) adder_2 (.a(multiplexer_4_out), .b(adder_1_out), .out(adder_2_out));  // open: cin, cout
  assign bit_extender_1_out = {{3{rom_1_data[15]}}, rom_1_data[15:3]};  // Bit_Extender bit_extender_1
  ControlUnit controlunit_1 (
    .OP(rom_1_data[2:0]), .funct(rom_1_data[15:12]), .MemRead(controlunit_1_memread),
    .RegDst(controlunit_1_regdst), .RegWrite(controlunit_1_regwrite), .AluSrc(controlunit_1_alusrc),
    .ExtOp(controlunit_1_extop), .MemToReg(controlunit_1_memtoreg), .MemWrite(controlunit_1_memwrite),
    .Branch(controlunit_1_branch), .Jump(controlunit_1_jump), .AluCtrl(controlunit_1_aluctrl));
  and Branch (Branch_out, alu_1_euality, controlunit_1_branch);
  Multiplexer #(.width(3), .enable("false")) multiplexer_3 (
    .in0(rom_1_data[8:6]), .in1(rom_1_data[11:9]), .out(multiplexer_3_out), .sel(controlunit_1_regdst));
  assign bit_extender_2_out = {{9{rom_1_data[15]}}, rom_1_data[15:9]};  // Bit_Extender bit_extender_2
  assign bit_extender_3_out = {{9{1'b0}}, rom_1_data[15:9]};  // Bit_Extender bit_extender_3
  RegisterFile registerfile_1 (
    .WriteBack_Data(multiplexer_6_out), .CLK(clock_1_out), .Reset(in_1), .Destination(multiplexer_3_out),
    .Reg1(rom_1_data[5:3]), .Reg2(rom_1_data[8:6]), .R_W(controlunit_1_regwrite),
    .OutReg1(registerfile_1_outreg1), .OutReg2(registerfile_1_outreg2));
  Multiplexer #(.width(16), .enable("false")) multiplexer_4 (
    .in0(bit_extender_3_out), .in1(bit_extender_2_out), .out(multiplexer_4_out), .sel(controlunit_1_extop));
  Multiplexer #(.width(16), .enable("false")) multiplexer_5 (
    .in0(registerfile_1_outreg2), .in1(multiplexer_4_out), .out(multiplexer_5_out), .sel(controlunit_1_alusrc));
  ALU alu_1 (
    .input1(registerfile_1_outreg1), .input2(multiplexer_5_out), .ALU_Control(controlunit_1_aluctrl),
    .ALU_Output(alu_1_alu_output), .Euality(alu_1_euality));
  RAM #(.addrWidth(16), .dataWidth(16), .bus("separate")) ram_1 (
    .addr(alu_1_alu_output), .din(registerfile_1_outreg2), .data(ram_1_data), .str(controlunit_1_memwrite),
    .clk(clock_1_out), .ld(controlunit_1_memread), .clr(in_2));  // open: sel
  Multiplexer #(.width(16), .enable("false")) multiplexer_6 (
    .in0(alu_1_alu_output), .in1(ram_1_data), .out(multiplexer_6_out), .sel(controlunit_1_memtoreg));

  // Notes on the sheet:
  //   contents of rom_1 (hex, n*v repeats v):
  //   990 991 2883 4883
  //   Jump
  //   shift left 2?
endmodule

// Conntrol Unit
module ControlUnit (
  input  [2:0] OP,
  input  [3:0] funct,
  output RegDst,
  output RegWrite,
  output MemRead,
  output AluSrc,
  output ExtOp,
  output MemToReg,
  output MemWrite,
  output Branch,
  output Jump,
  output [2:0] AluCtrl
);

  wire addi_out, and_1_out, and_2_out, andi_out, not_1_out, not_2_out, not_3_out, not_4_out, not_5_out,
       not_6_out, not_7_out, not_8_out, not_9_out, not_10_out, not_11_out, not_12_out, not_13_out,
       not_14_out, not_15_out, not_16_out, ori_out;
  wire [1:0] bit_extender_2_out;
  wire [2:0] bit_extender_1_out, bit_extender_3_out;

  Bit_Extender #(.in_width(4), .out_width(3)) bit_extender_1 (.in(funct), .out(bit_extender_1_out));
  assign bit_extender_2_out = {{1{and_2_out}}, and_1_out};  // Bit_Extender bit_extender_2
  not not_1 (not_1_out, OP[2]);
  not not_2 (not_2_out, OP[1]);
  and R_type (RegDst, not_1_out, not_2_out, not_3_out);
  not not_3 (not_3_out, OP[0]);
  not not_4 (not_4_out, OP[2]);
  and load (MemRead, not_4_out, not_5_out, OP[0]);
  not not_5 (not_5_out, OP[1]);
  not not_6 (not_6_out, OP[2]);
  and store (MemWrite, not_6_out, OP[1], not_7_out);
  not not_7 (not_7_out, OP[0]);
  not not_8 (not_8_out, OP[2]);
  and beq (Branch, not_8_out, OP[1], OP[0]);
  and addi (addi_out, OP[2], not_9_out, not_10_out);
  not not_9 (not_9_out, OP[1]);
  not not_10 (not_10_out, OP[0]);
  not not_11 (not_11_out, OP[1]);
  and andi (andi_out, OP[2], not_11_out, OP[0]);
  and ori (ori_out, OP[2], OP[1], not_12_out);
  not not_12 (not_12_out, OP[0]);
  and u_jump (Jump, OP[2], OP[1], OP[0]);
  not not_13 (not_13_out, Branch);
  not not_14 (not_14_out, andi_out);
  and and_1 (and_1_out, not_14_out, not_13_out);
  assign bit_extender_3_out = {{1{Branch}}, bit_extender_2_out};  // Bit_Extender bit_extender_3
  not not_15 (not_15_out, ori_out);
  not not_16 (not_16_out, Branch);
  and and_2 (and_2_out, not_16_out, not_15_out);
  Multiplexer #(.width(3), .enable("false")) multiplexer_1 (
    .in0(bit_extender_3_out), .in1(bit_extender_1_out), .out(AluCtrl), .sel(RegDst));
  or or_1 (RegWrite, RegDst, addi_out, andi_out, ori_out, MemRead);
  or or_2 (AluSrc, MemRead, addi_out, andi_out, ori_out, MemWrite);
  or or_3 (ExtOp, MemRead, MemWrite);

  assign MemToReg = MemRead;

  // Notes on the sheet:
  //   ================================
  //   AluControlUnit
  //   ====================================
  //   MainControlUnit
endmodule

module ALU (
  input  [2:0] ALU_Control,
  input  [15:0] input1,
  input  [15:0] input2,
  output [15:0] ALU_Output,
  output Euality
);

  wire [15:0] adder_1_out, AND_out, divider_1_out, multiplier_1_out, NAND_out, OR_out, subtractor_1_out,
       XOR_out;

  Comparator #(.width(16)) comparator_1 (.a(input1), .b(input2), .eq(Euality));  // open: gt, lt
  assign XOR_out = input1 ^ input2;  // XOR_Gate XOR, 16 bits wide
  assign OR_out = input1 | input2;  // OR_Gate OR, 16 bits wide
  assign AND_out = input1 & input2;  // AND_Gate AND, 16 bits wide
  Adder #(.width(16)) adder_1 (.a(input1), .b(input2), .out(adder_1_out));  // open: cin, cout
  Subtractor #(.width(16)) subtractor_1 (.a(input1), .b(input2), .out(subtractor_1_out));  // open: bin, bout
  Divider #(.width(16)) divider_1 (.a(input1), .b(input2), .out(divider_1_out));  // open: upper, rem
  Multiplier #(.width(16)) multiplier_1 (.a(input1), .b(input2), .out(multiplier_1_out));  // open: cin, cout
  assign NAND_out = ~(input1 & input2);  // NAND_Gate NAND, 16 bits wide
  Multiplexer #(.select(3), .width(16), .enable("false")) multiplexer_1 (
    .in0(XOR_out), .in1(OR_out), .in2(AND_out), .in3(adder_1_out), .in4(subtractor_1_out),
    .in5(divider_1_out), .in6(multiplier_1_out), .in7(NAND_out), .out(ALU_Output), .sel(ALU_Control));
endmodule

// Register file
module RegisterFile (
  input  [15:0] WriteBack_Data,
  input  CLK,
  input  Reset,
  input  [2:0] Destination,
  input  [2:0] Reg1,
  input  [2:0] Reg2,
  input  R_W,
  output [15:0] OutReg1,
  output [15:0] OutReg2
);

  wire and_1_out, and_2_out, and_3_out, and_4_out, and_5_out, and_6_out, and_7_out, and_8_out,
       demultiplexer_1_out0, demultiplexer_1_out1, demultiplexer_1_out2, demultiplexer_1_out3,
       demultiplexer_1_out4, demultiplexer_1_out5, demultiplexer_1_out6, demultiplexer_1_out7;
  wire [15:0] Reg0_q, Reg1_q, Reg2_q, Reg3_q, Reg4_q, Reg5_q, Reg6_q, Reg7_q, register_1_q;

  Register #(.width(16)) register_1 (.D(WriteBack_Data), .Q(register_1_q), .clk(CLK), .clr(Reset));  // open: en
  Demultiplexer #(.select(3), .enable("false")) demultiplexer_1 (
    .out0(demultiplexer_1_out0), .out1(demultiplexer_1_out1), .out2(demultiplexer_1_out2),
    .out3(demultiplexer_1_out3), .out4(demultiplexer_1_out4), .out5(demultiplexer_1_out5),
    .out6(demultiplexer_1_out6), .out7(demultiplexer_1_out7), .in(1'b1), .sel(Destination));
  and and_1 (and_1_out, demultiplexer_1_out0, R_W);
  and and_2 (and_2_out, demultiplexer_1_out1, R_W);
  and and_3 (and_3_out, demultiplexer_1_out2, R_W);
  and and_4 (and_4_out, demultiplexer_1_out3, R_W);
  and and_5 (and_5_out, demultiplexer_1_out4, R_W);
  and and_6 (and_6_out, demultiplexer_1_out5, R_W);
  and and_7 (and_7_out, demultiplexer_1_out6, R_W);
  and and_8 (and_8_out, demultiplexer_1_out7, R_W);
  Register #(.width(16), .trigger("high")) Reg0 (
    .D(register_1_q), .Q(Reg0_q), .clk(and_1_out), .clr(Reset));  // open: en
  Register #(.width(16), .trigger("high")) u_Reg1 (
    .D(register_1_q), .Q(Reg1_q), .clk(and_2_out), .clr(Reset));  // open: en
  Register #(.width(16), .trigger("high")) u_Reg2 (
    .D(register_1_q), .Q(Reg2_q), .clk(and_3_out), .clr(Reset));  // open: en
  Register #(.width(16), .trigger("high")) Reg3 (
    .D(register_1_q), .Q(Reg3_q), .clk(and_4_out), .clr(Reset));  // open: en
  Register #(.width(16), .trigger("high")) Reg4 (
    .D(register_1_q), .Q(Reg4_q), .clk(and_5_out), .clr(Reset));  // open: en
  Register #(.width(16), .trigger("high")) Reg5 (
    .D(register_1_q), .Q(Reg5_q), .clk(and_6_out), .clr(Reset));  // open: en
  Register #(.width(16), .trigger("high")) Reg6 (
    .D(register_1_q), .Q(Reg6_q), .clk(and_7_out), .clr(Reset));  // open: en
  Register #(.width(16), .trigger("high")) Reg7 (
    .D(register_1_q), .Q(Reg7_q), .clk(and_8_out), .clr(Reset));  // open: en
  Multiplexer #(.select(3), .width(16), .enable("false")) multiplexer_1 (
    .in0(Reg0_q), .in1(Reg1_q), .in2(Reg2_q), .in3(Reg3_q), .in4(Reg4_q), .in5(Reg5_q), .in6(Reg6_q),
    .in7(Reg7_q), .out(OutReg1), .sel(Reg1));
  Multiplexer #(.select(3), .width(16), .enable("false")) multiplexer_2 (
    .in0(Reg0_q), .in1(Reg1_q), .in2(Reg2_q), .in3(Reg3_q), .in4(Reg4_q), .in5(Reg5_q), .in6(Reg6_q),
    .in7(Reg7_q), .out(OutReg2), .sel(Reg2));
endmodule
